// Digital circuit Processador_projeto2va.dig as structural Verilog
module Processador_projeto2va (
  input  Clk,
  input  nRst,
  input  [4:0] RbAdd,
  input  nHalt
);

  wire and_2_out, Clk_t, not_1_out, u_control_alusrc, u_control_branch, u_control_memtoreg,
       u_control_memwrite, u_control_regdst, u_control_regwrite, u_ULA_zero;
  wire [4:0] Rd, RegWr, Rs, Rt, u_control_aluop, ULA_Op;
  wire [7:0] u_RegistradorPC_y_2;
  wire [10:0] ROM_d;
  wire [31:0] DMEM_d, Rb, u_BancoReg_rddata2, u_ExtensorSinal_y, u_Mux2x1_32bits_y, u_RegistradorPC_y,
       u_Soma4_y, u_somaPcDesvio_enderecodesvio, ULA_R1, ULA_R2, ULA_Result, WrData;
  wire [31:26] ROM_d_2;

  // Probe RbAdd on RbAdd
  // Probe Rb on Rb
  // Probe Rs on Rs
  // Probe Rt on Rt
  // Probe Rd on Rd
  // Probe RegWr on RegWr
  // Probe ULA_2 on ULA_R2
  // Probe Ula_1 on ULA_R1
  // Probe ResultULA on ULA_Result
  // Probe WrData on WrData
  // Probe ULA_op on ULA_Op
  // ScopeTrigger #(.maxStepCount(100)) scopetrigger_1: pin names not known; wires that end beside it: Clk_t
  Seven_Seg_Hex seven_seg_hex_1 (.d({3'b000, RbAdd[4]}), .dp(1'b0));
  Seven_Seg_Hex seven_seg_hex_2 (.d(RbAdd[3:0]), .dp(1'b0));
  // Probe Endereço on u_Mux2x1_32bits_y
  RegistradorPC #(.applicationType("IVERILOG")) u_RegistradorPC (
    .A(u_Mux2x1_32bits_y), .Clk(Clk_t), .Rst(nRst),
    .Y({u_RegistradorPC_y[31:10], u_RegistradorPC_y_2, u_RegistradorPC_y[1:0]}));
  and and_1 (Clk_t, Clk, nHalt);
  Seven_Seg_Hex seven_seg_hex_3 (.d(Rb[31:28]), .dp(1'b0));
  Soma4 #(.applicationType("IVERILOG")) u_Soma4 (
    .A({u_RegistradorPC_y[31:10], u_RegistradorPC_y_2, u_RegistradorPC_y[1:0]}), .Y(u_Soma4_y));
  Seven_Seg_Hex seven_seg_hex_4 (.d(Rb[27:24]), .dp(1'b0));
  Mux2x1_32bits #(.applicationType("IVERILOG")) u_Mux2x1_32bits (
    .A(u_Soma4_y), .B(u_somaPcDesvio_enderecodesvio), .S(and_2_out), .Y(u_Mux2x1_32bits_y));
  ROM #(.bigEndian("true"), .AddrBits(8), .isProgramMemory("true"), .Bits(32)) ROM (
    .A(u_RegistradorPC_y_2), .sel(1'b1), .D({ROM_d_2, Rs, Rt, Rd, ROM_d}));
  Seven_Seg_Hex seven_seg_hex_5 (.d(Rb[23:20]), .dp(1'b0));
  and and_2 (and_2_out, u_ULA_zero, u_control_branch);
  // Probe Instrução on {ROM_d_2, Rs, Rt, Rd, ROM_d}
  control #(.applicationType("IVERILOG")) u_control (
    .instruction({ROM_d_2, Rs, Rt, Rd, ROM_d}), .RegDst(u_control_regdst), .MemtoReg(u_control_memtoreg),
    .ALUSrc(u_control_alusrc), .Branch(u_control_branch), .MemWrite(u_control_memwrite),
    .RegWrite(u_control_regwrite), .ALUOp(u_control_aluop));
  Seven_Seg_Hex seven_seg_hex_6 (.d(Rb[19:16]), .dp(1'b0));
  Seven_Seg_Hex seven_seg_hex_7 (.d(Rb[15:12]), .dp(1'b0));
  ExtensorSinal #(.applicationType("IVERILOG")) u_ExtensorSinal (.A({Rd, ROM_d}), .Y(u_ExtensorSinal_y));
  Seven_Seg_Hex seven_seg_hex_8 (.d(Rb[11:8]), .dp(1'b0));
  Seven_Seg_Hex seven_seg_hex_9 (.d(Rb[7:4]), .dp(1'b0));
  Seven_Seg_Hex seven_seg_hex_10 (.d(Rb[3:0]), .dp(1'b0));
  mux2x1_5bits #(.applicationType("IVERILOG")) u_mux2x1_5bits (.S(u_control_regdst), .A(Rt), .B(Rd), .Y(RegWr));
  BancoReg #(.applicationType("IVERILOG")) u_BancoReg (
    .RegRd1(Rs), .RegRd2(Rt), .RegWr(RegWr), .WrData(WrData), .Write(u_control_regwrite), .rst(nRst),
    .clk(Clk_t), .RbAdd(RbAdd), .RdData1(ULA_R1), .RdData2(u_BancoReg_rddata2), .Rb(Rb));
  somaPcDesvio #(.applicationType("IVERILOG")) u_somaPcDesvio (
    .endereco(u_Soma4_y), .desvio(u_ExtensorSinal_y), .enderecoDesvio(u_somaPcDesvio_enderecodesvio));
  ALU_control #(.applicationType("IVERILOG")) u_ALU_control (.ALUOp(u_control_aluop), .ALU_control_vector(ULA_Op));
  Mux2x1_32bits #(.applicationType("IVERILOG")) u_Mux2x1_32bits_2 (
    .S(u_control_alusrc), .A(u_BancoReg_rddata2), .B(u_ExtensorSinal_y), .Y(ULA_R2));
  ULA #(.applicationType("IVERILOG")) u_ULA (.A(ULA_R1), .B(ULA_R2), .Op(ULA_Op), .zero(u_ULA_zero), .Y(ULA_Result));
  not not_1 (not_1_out, Clk_t);
  BlockRAMDualPort #(.AddrBits(8), .isProgramMemory("true"), .Bits(32)) DMEM (
    .A(ULA_Result[7:0]), .Din(u_BancoReg_rddata2), .str(u_control_memwrite), .C(not_1_out), .D(DMEM_d));
  Mux2x1_32bits #(.applicationType("IVERILOG")) u_Mux2x1_32bits_3 (
    .S(u_control_memtoreg), .A(ULA_Result), .B(DMEM_d), .Y(WrData));

  // Notes on the sheet:
  //   contents of ROM (hex, n*v repeats v):
  //   20080005,20090003,1095020
endmodule

/* Code of RegistradorPC:
module RegistradorPC(
    input      [31:0] A,
    input             Clk,
    input             Rst,
    output reg [31:0] Y
);

    always @(posedge Clk or negedge Rst) begin
        if (!Rst)
            Y <= 32'd0;
        else
            Y <= A;
    end

endmodule
*/

/* Code of Soma4:
module Soma4(
    input  [31:0] A,
    output [31:0] Y
);

    assign Y = A + 32'd4;

endmodule
*/

/* Code of Mux2x1_32bits:
module Mux2x1_32bits(
    input         S,
    input  [31:0] A,
    input  [31:0] B,
    output [31:0] Y
);

    assign Y = S ? B : A;

endmodule
*/

/* Code of control:
module control(
    input [31:0] instruction,
    output reg RegDst,
    output reg MemtoReg,
    output reg ALUSrc,
    output reg Branch,
    output reg MemWrite,
    output reg RegWrite,
    output reg [4:0] ALUOp
);

    wire [5:0] opcode;
    wire [5:0] funct;

    assign opcode = instruction[31:26];
    assign funct  = instruction[5:0];

    always @(*) begin
        RegDst   = 1'b0;
        MemtoReg = 1'b0;
        ALUSrc   = 1'b0;
        Branch   = 1'b0;
        MemWrite = 1'b0;
        RegWrite = 1'b0;
        ALUOp    = 5'b00000;

        case (opcode)
            // Instrucoes tipo R
            6'b000000: begin
                RegDst = 1'b1;

                case (funct)
                    6'b100000: begin // add
                        RegWrite = 1'b1;
                        ALUOp = 5'b00000;
                    end

                    6'b100010: begin // sub
                        RegWrite = 1'b1;
                        ALUOp = 5'b00001;
                    end

                    6'b100100: begin // and
                        RegWrite = 1'b1;
                        ALUOp = 5'b00010;
                    end

                    6'b100101: begin // or
                        RegWrite = 1'b1;
                        ALUOp = 5'b00011;
                    end

                    6'b000100: begin // sllv
                        RegWrite = 1'b1;
                        ALUOp = 5'b00100;
                    end

                    6'b000110: begin // srlv
                        RegWrite = 1'b1;
                        ALUOp = 5'b00101;
                    end

                    default: begin
                        RegWrite = 1'b0;
                    end
                endcase
            end

            6'b001000: begin // addi
                ALUSrc   = 1'b1;
                RegWrite = 1'b1;
                ALUOp    = 5'b00000;
            end

            6'b001101: begin // ori
                ALUSrc   = 1'b1;
                RegWrite = 1'b1;
                ALUOp    = 5'b00110;
            end

            6'b100011: begin // lw
                ALUSrc   = 1'b1;
                MemtoReg = 1'b1;
                RegWrite = 1'b1;
                ALUOp    = 5'b00000;
            end

            6'b101011: begin // sw
                ALUSrc   = 1'b1;
                MemWrite = 1'b1;
                ALUOp    = 5'b00000;
            end

            6'b000100: begin // beq
                Branch = 1'b1;
                ALUOp  = 5'b00001;
            end

            default: begin
                // Instrucao nao suportada:
                // mantem os valores padrao, sem escrita.
            end
        endcase
    end

endmodule
*/

/* Code of ExtensorSinal:
module ExtensorSinal(
    input  [15:0] A,
    output [31:0] Y
);

    assign Y = {{16{A[15]}}, A};

endmodule
*/

/* Code of mux2x1_5bits:
module mux2x1_5bits(
    input        S,
    input  [4:0] A,
    input  [4:0] B,
    output [4:0] Y
);

    assign Y = S ? B : A;

endmodule
*/

/* Code of BancoReg:
module BancoReg(
    input  [4:0]  RegRd1,
    input  [4:0]  RegRd2,
    input  [4:0]  RegWr,
    input  [31:0] WrData,
    input         Write,
    input         rst,
    input         clk,
    input  [4:0]  RbAdd,
    output [31:0] RdData1,
    output [31:0] RdData2,
    output [31:0] Rb
);

    reg [31:0] registradores [0:31];
    integer i;

    always @(posedge clk or negedge rst) begin
        if (!rst) begin
            for (i = 0; i < 32; i = i + 1)
                registradores[i] <= 32'd0;
        end
        else if (Write && RegWr != 5'd0) begin
            registradores[RegWr] <= WrData;
        end
    end

    assign RdData1 = (RegRd1 == 5'd0)
                   ? 32'd0 : registradores[RegRd1];

    assign RdData2 = (RegRd2 == 5'd0)
                   ? 32'd0 : registradores[RegRd2];

    assign Rb = (RbAdd == 5'd0)
              ? 32'd0 : registradores[RbAdd];

endmodule
*/

/* Code of somaPcDesvio:
module somaPcDesvio(
    input  [31:0] endereco,
    input  [31:0] desvio,
    output [31:0] enderecoDesvio
);

    assign enderecoDesvio = endereco + (desvio << 2);

endmodule
*/

/* Code of ALU_control:
module ALU_control(
    input  [4:0] ALUOp,
    output [4:0] ALU_control_vector
);

    assign ALU_control_vector = ALUOp;

endmodule
*/

/* Code of ULA:
module ULA(
    input  [31:0] A,
    input  [31:0] B,
    input  [4:0]  Op,
    output        zero,
    output reg [31:0] Y
);

    always @(*) begin
        case (Op)
            5'b00000: Y = A + B;
            5'b00001: Y = A - B;
            5'b00010: Y = A & B;
            5'b00011: Y = A | B;
            5'b00100: Y = B << A[4:0];
            5'b00101: Y = B >> A[4:0];
            5'b00110: Y = A | {16'b0, B[15:0]};
            default:  Y = 32'd0;
        endcase
    end

    assign zero = (Y == 32'd0);

endmodule
*/
